// Logisim project MUX.circ as structural Verilog: 4 circuits, main circuit MUX
module MUX (
  input  R,
  input  Q,
  input  P
);

  wire multiplexer_1_out, multiplexer_2_out, multiplexer_3_out, multiplexer_4_out, multiplexer_5_out,
       multiplexer_6_out, multiplexer_7_out, not_1_out, not_2_out, not_3_out, not_4_out;

  not not_1 (not_1_out, 1'b0);
  not not_2 (not_2_out, 1'b0);
  not not_3 (not_3_out, 1'b0);
  not not_4 (not_4_out, R);
  Multiplexer #(.select(2), .enable("false")) multiplexer_1 (
    .in0(not_4_out), .in1(not_1_out), .in2(1'b0), .in3(not_4_out), .out(multiplexer_1_out), .sel({P, Q}));
  Multiplexer #(.select(2), .enable("false")) multiplexer_2 (
    .in0(1'b0), .in1(not_1_out), .in2(1'b0), .in3(not_4_out), .out(multiplexer_2_out), .sel({P, Q}));
  Multiplexer #(.select(2), .enable("false")) multiplexer_3 (
    .in0(1'b0), .in1(not_1_out), .in2(1'b0), .in3(not_4_out), .out(multiplexer_3_out), .sel({P, Q}));
  Multiplexer #(.select(2), .enable("false")) multiplexer_4 (
    .in0(R), .in1(not_1_out), .in2(1'b0), .in3(not_4_out), .out(multiplexer_4_out), .sel({P, Q}));
  Multiplexer #(.select(2), .enable("false")) multiplexer_5 (
    .in0(not_2_out), .in1(not_1_out), .in2(not_4_out), .in3(1'b0), .out(multiplexer_5_out), .sel({P, Q}));
  Multiplexer #(.select(2), .enable("false")) multiplexer_6 (
    .in0(not_2_out), .in1(not_1_out), .in2(1'b0), .in3(not_4_out), .out(multiplexer_6_out), .sel({P, Q}));
  Multiplexer #(.select(2), .enable("false")) multiplexer_7 (
    .in0(not_4_out), .in1(1'b0), .in2(not_3_out), .in3(not_4_out), .out(multiplexer_7_out), .sel({P, Q}));
  _7_Segment_Display u_7_segment_display_1 (
    .g(multiplexer_7_out), .f(multiplexer_6_out), .a(multiplexer_1_out), .b(multiplexer_2_out),
    .e(multiplexer_5_out), .d(multiplexer_4_out), .c(multiplexer_3_out));  // open: dp

  // Notes on the sheet:
  //   I1
  //   I2
  //   I4
  //   I3
endmodule

module MUX_using__D_Flip_Flop (
  input  Switch
);

  wire and_1_out, and_2_out, and_3_out, and_4_out, and_5_out, and_6_out, and_7_out, and_8_out, button_1_out,
       Clock_out, DP_qn, DQ_qn, DR_q, DR_qn, multiplexer_1_out, multiplexer_2_out, multiplexer_3_out,
       multiplexer_4_out, multiplexer_5_out, multiplexer_6_out, multiplexer_7_out, not_1_out, not_2_out,
       not_3_out, not_4_out, or_1_out, or_2_out, or_3_out;
  wire [1:0] DQ_q;

  and and_1 (and_1_out, DP_qn, DQ_q[0], DR_q);
  and and_2 (and_2_out, DQ_q[1], DQ_qn);
  and and_3 (and_3_out, DQ_q[1], DR_qn);
  and and_4 (and_4_out, DQ_qn, DR_q);
  and and_5 (and_5_out, DQ_q[0], DR_qn);
  or or_1 (or_1_out, and_1_out, and_2_out, and_3_out);
  and and_6 (and_6_out, DQ_qn, DR_qn);
  and and_7 (and_7_out, DQ_q[0], DR_qn);
  Clock Clock (.out(Clock_out));
  or or_2 (or_2_out, and_4_out, and_5_out);
  or or_3 (or_3_out, and_6_out, and_7_out);
  and and_8 (and_8_out, Clock_out, Switch);
  D_Flip_Flop DP (.clk(and_8_out), .D(or_1_out), .Q(DQ_q[1]), .Qn(DP_qn), .reset(button_1_out));  // open: preset, en
  D_Flip_Flop DQ (.clk(and_8_out), .D(or_2_out), .Q(DQ_q[0]), .Qn(DQ_qn), .reset(button_1_out));  // open: preset, en
  D_Flip_Flop DR (.clk(and_8_out), .D(or_3_out), .Q(DR_q), .Qn(DR_qn), .reset(button_1_out));  // open: preset, en
  Button button_1 (.out(button_1_out));
  not not_1 (not_1_out, 1'b0);
  not not_2 (not_2_out, 1'b0);
  not not_3 (not_3_out, 1'b0);
  not not_4 (not_4_out, DR_q);
  Multiplexer #(.select(2), .enable("false")) multiplexer_1 (
    .in0(not_4_out), .in1(not_1_out), .in2(1'b0), .in3(not_4_out), .out(multiplexer_1_out), .sel(DQ_q));
  Multiplexer #(.select(2), .enable("false")) multiplexer_2 (
    .in0(1'b0), .in1(not_1_out), .in2(1'b0), .in3(not_4_out), .out(multiplexer_2_out), .sel(DQ_q));
  Multiplexer #(.select(2), .enable("false")) multiplexer_3 (
    .in0(1'b0), .in1(not_1_out), .in2(1'b0), .in3(not_4_out), .out(multiplexer_3_out), .sel(DQ_q));
  Multiplexer #(.select(2), .enable("false")) multiplexer_4 (
    .in0(DR_q), .in1(not_1_out), .in2(1'b0), .in3(not_4_out), .out(multiplexer_4_out), .sel(DQ_q));
  Multiplexer #(.select(2), .enable("false")) multiplexer_5 (
    .in0(not_2_out), .in1(not_1_out), .in2(not_4_out), .in3(1'b0), .out(multiplexer_5_out), .sel(DQ_q));
  Multiplexer #(.select(2), .enable("false")) multiplexer_6 (
    .in0(not_2_out), .in1(not_1_out), .in2(1'b0), .in3(not_4_out), .out(multiplexer_6_out), .sel(DQ_q));
  Multiplexer #(.select(2), .enable("false")) multiplexer_7 (
    .in0(not_4_out), .in1(1'b0), .in2(not_3_out), .in3(not_4_out), .out(multiplexer_7_out), .sel(DQ_q));
  _7_Segment_Display u_7_segment_display_1 (
    .g(multiplexer_7_out), .f(multiplexer_6_out), .a(multiplexer_1_out), .b(multiplexer_2_out),
    .e(multiplexer_5_out), .d(multiplexer_4_out), .c(multiplexer_3_out));  // open: dp

  // Notes on the sheet:
  //   I2
  //   I3
  //   I4
endmodule

module MUX_using__T_Flip_Flop (
  input  Switch
);

  wire and_1_out, and_2_out, button_1_out, Clock_out, multiplexer_1_out, multiplexer_2_out,
       multiplexer_3_out, multiplexer_4_out, multiplexer_5_out, multiplexer_6_out, multiplexer_7_out,
       not_1_out, not_2_out, not_3_out, not_4_out, TR_q;
  wire [1:0] TQ_q;

  and and_1 (and_1_out, TQ_q[0], TR_q);
  T_Flip_Flop TP (.clk(and_2_out), .T(and_1_out), .Q(TQ_q[1]), .reset(button_1_out));  // open: Qn, preset, en
  T_Flip_Flop TQ (.clk(and_2_out), .T(TR_q), .Q(TQ_q[0]), .reset(button_1_out));  // open: Qn, preset, en
  T_Flip_Flop TR (.clk(and_2_out), .T(1'b1), .Q(TR_q), .reset(button_1_out));  // open: Qn, preset, en
  Button button_1 (.out(button_1_out));
  and and_2 (and_2_out, Clock_out, Switch);
  Clock #(.highDuration(3), .lowDuration(2)) Clock (.out(Clock_out));
  not not_1 (not_1_out, 1'b0);
  not not_2 (not_2_out, 1'b0);
  not not_3 (not_3_out, 1'b0);
  not not_4 (not_4_out, TR_q);
  Multiplexer #(.select(2), .enable("false")) multiplexer_1 (
    .in0(not_4_out), .in1(not_1_out), .in2(1'b0), .in3(not_4_out), .out(multiplexer_1_out), .sel(TQ_q));
  Multiplexer #(.select(2), .enable("false")) multiplexer_2 (
    .in0(1'b0), .in1(not_1_out), .in2(1'b0), .in3(not_4_out), .out(multiplexer_2_out), .sel(TQ_q));
  Multiplexer #(.select(2), .enable("false")) multiplexer_3 (
    .in0(1'b0), .in1(not_1_out), .in2(1'b0), .in3(not_4_out), .out(multiplexer_3_out), .sel(TQ_q));
  Multiplexer #(.select(2), .enable("false")) multiplexer_4 (
    .in0(TR_q), .in1(not_1_out), .in2(1'b0), .in3(not_4_out), .out(multiplexer_4_out), .sel(TQ_q));
  Multiplexer #(.select(2), .enable("false")) multiplexer_5 (
    .in0(not_2_out), .in1(not_1_out), .in2(not_4_out), .in3(1'b0), .out(multiplexer_5_out), .sel(TQ_q));
  Multiplexer #(.select(2), .enable("false")) multiplexer_6 (
    .in0(not_2_out), .in1(not_1_out), .in2(1'b0), .in3(not_4_out), .out(multiplexer_6_out), .sel(TQ_q));
  Multiplexer #(.select(2), .enable("false")) multiplexer_7 (
    .in0(not_4_out), .in1(1'b0), .in2(not_3_out), .in3(not_4_out), .out(multiplexer_7_out), .sel(TQ_q));
  _7_Segment_Display u_7_segment_display_1 (
    .g(multiplexer_7_out), .f(multiplexer_6_out), .a(multiplexer_1_out), .b(multiplexer_2_out),
    .e(multiplexer_5_out), .d(multiplexer_4_out), .c(multiplexer_3_out));  // open: dp

  // Notes on the sheet:
  //   I1
  //   I2
  //   I4
  //   I3
endmodule

module MUX_using__JK_Flip_Flop (
  input  Switch
);

  wire and_1_out, and_2_out, and_3_out, button_1_out, Clock_out, j_k_ff_3_q, multiplexer_1_out,
       multiplexer_2_out, multiplexer_3_out, multiplexer_4_out, multiplexer_5_out, multiplexer_6_out,
       multiplexer_7_out, not_1_out, not_2_out, not_3_out, not_4_out;
  wire [1:0] j_k_ff_2_q;

  and and_1 (and_1_out, j_k_ff_2_q[0], j_k_ff_3_q);
  and and_2 (and_2_out, j_k_ff_2_q[0], j_k_ff_3_q);
  and and_3 (and_3_out, Clock_out, Switch);
  J_K_Flip_Flop j_k_ff_1 (
    .J(and_1_out), .clk(and_3_out), .K(and_2_out), .Q(j_k_ff_2_q[1]), .reset(button_1_out));  // open: Qn, preset, en
  J_K_Flip_Flop j_k_ff_2 (
    .J(j_k_ff_3_q), .clk(and_3_out), .K(j_k_ff_3_q), .Q(j_k_ff_2_q[0]), .reset(button_1_out));  // open: Qn, preset, en
  J_K_Flip_Flop j_k_ff_3 (
    .J(1'b1), .clk(and_3_out), .K(1'b1), .Q(j_k_ff_3_q), .reset(button_1_out));  // open: Qn, preset, en
  Button button_1 (.out(button_1_out));
  Clock #(.highDuration(3), .lowDuration(2)) Clock (.out(Clock_out));
  not not_1 (not_1_out, 1'b0);
  not not_2 (not_2_out, 1'b0);
  not not_3 (not_3_out, 1'b0);
  not not_4 (not_4_out, j_k_ff_3_q);
  Multiplexer #(.select(2), .enable("false")) multiplexer_1 (
    .in0(not_4_out), .in1(not_1_out), .in2(1'b0), .in3(not_4_out), .out(multiplexer_1_out), .sel(j_k_ff_2_q));
  Multiplexer #(.select(2), .enable("false")) multiplexer_2 (
    .in0(1'b0), .in1(not_1_out), .in2(1'b0), .in3(not_4_out), .out(multiplexer_2_out), .sel(j_k_ff_2_q));
  Multiplexer #(.select(2), .enable("false")) multiplexer_3 (
    .in0(1'b0), .in1(not_1_out), .in2(1'b0), .in3(not_4_out), .out(multiplexer_3_out), .sel(j_k_ff_2_q));
  Multiplexer #(.select(2), .enable("false")) multiplexer_4 (
    .in0(j_k_ff_3_q), .in1(not_1_out), .in2(1'b0), .in3(not_4_out), .out(multiplexer_4_out), .sel(j_k_ff_2_q));
  Multiplexer #(.select(2), .enable("false")) multiplexer_5 (
    .in0(not_2_out), .in1(not_1_out), .in2(not_4_out), .in3(1'b0), .out(multiplexer_5_out), .sel(j_k_ff_2_q));
  Multiplexer #(.select(2), .enable("false")) multiplexer_6 (
    .in0(not_2_out), .in1(not_1_out), .in2(1'b0), .in3(not_4_out), .out(multiplexer_6_out), .sel(j_k_ff_2_q));
  Multiplexer #(.select(2), .enable("false")) multiplexer_7 (
    .in0(not_4_out), .in1(1'b0), .in2(not_3_out), .in3(not_4_out), .out(multiplexer_7_out), .sel(j_k_ff_2_q));
  _7_Segment_Display u_7_segment_display_1 (
    .g(multiplexer_7_out), .f(multiplexer_6_out), .a(multiplexer_1_out), .b(multiplexer_2_out),
    .e(multiplexer_5_out), .d(multiplexer_4_out), .c(multiplexer_3_out));  // open: dp

  // Notes on the sheet:
  //   JP
  //   KP
  //   JQ
  //   KQ
  //   JR
  //   KR
  //   I1
  //   I2
  //   I3
  //   I4
endmodule
