// Logisim project basic_project.circ as structural Verilog: 4 circuits, main circuit Basic gate
module Basic_gate (
  input  P,
  input  Q,
  input  R
);

  wire and_1_out, and_2_out, and_3_out, and_4_out, and_5_out, and_6_out, and_7_out, and_8_out, and_9_out,
       and_10_out, and_11_out, and_12_out, and_13_out, and_14_out, not_1_out, not_2_out, not_3_out, or_1_out,
       or_2_out, or_3_out, or_4_out, or_5_out, or_6_out, or_7_out;

  not not_1 (not_1_out, P);
  not not_2 (not_2_out, Q);
  not not_3 (not_3_out, R);
  and and_1 (and_1_out, not_2_out, not_3_out);
  and and_2 (and_2_out, Q, not_3_out);
  and and_3 (and_3_out, not_1_out, not_3_out);
  and and_4 (and_4_out, not_1_out, Q);
  and and_5 (and_5_out, Q, not_3_out);
  and and_6 (and_6_out, not_1_out, Q);
  and and_7 (and_7_out, Q, not_3_out);
  and and_8 (and_8_out, not_1_out, Q);
  and and_9 (and_9_out, Q, not_3_out);
  and and_10 (and_10_out, not_1_out, R);
  and and_11 (and_11_out, Q, not_3_out);
  or or_1 (or_1_out, not_1_out, and_1_out);
  or or_2 (or_2_out, not_1_out, and_2_out);
  and and_12 (and_12_out, not_2_out, not_3_out);
  and and_13 (and_13_out, P, not_2_out);
  and and_14 (and_14_out, P, not_3_out);
  or or_3 (or_3_out, and_3_out, and_4_out, and_5_out);
  or or_4 (or_4_out, and_6_out, and_7_out);
  or or_5 (or_5_out, and_12_out, and_13_out, and_14_out);
  or or_6 (or_6_out, and_8_out, and_9_out);
  or or_7 (or_7_out, and_10_out, and_11_out);
  _7_Segment_Display u_7_segment_display_1 (
    .g(or_5_out), .f(or_2_out), .a(or_3_out), .b(or_4_out), .e(or_1_out), .d(or_7_out), .c(or_6_out));  // open: dp
endmodule

module Basic_gate_using__D_Flip_Flop (
  input  Switch
);

  wire and_1_out, and_2_out, and_3_out, and_4_out, and_5_out, and_6_out, and_7_out, and_8_out, and_9_out,
       and_10_out, and_11_out, and_12_out, and_13_out, and_14_out, and_15_out, and_16_out, and_17_out,
       and_18_out, and_19_out, and_20_out, and_21_out, and_22_out, button_1_out, Clock_out, DP_q, DP_qn,
       DQ_q, DQ_qn, DR_q, DR_qn, not_1_out, not_2_out, not_3_out, or_1_out, or_2_out, or_3_out, or_4_out,
       or_5_out, or_6_out, or_7_out, or_8_out, or_9_out, or_10_out;

  and and_1 (and_1_out, DP_qn, DQ_q, DR_q);
  and and_2 (and_2_out, DP_q, DQ_qn);
  and and_3 (and_3_out, DP_q, DR_qn);
  or or_1 (or_1_out, and_1_out, and_2_out, and_3_out);
  and and_4 (and_4_out, DQ_qn, DR_q);
  and and_5 (and_5_out, DQ_q, DR_qn);
  and and_6 (and_6_out, DQ_qn, DR_qn);
  or or_2 (or_2_out, and_6_out, and_7_out);
  and and_7 (and_7_out, DQ_q, DR_qn);
  Clock #(.highDuration(3), .lowDuration(2)) Clock (.out(Clock_out));
  or or_3 (or_3_out, and_4_out, and_5_out);
  and and_8 (and_8_out, Clock_out, Switch);
  D_Flip_Flop DP (.clk(and_8_out), .D(or_1_out), .Q(DP_q), .Qn(DP_qn), .reset(button_1_out));  // open: preset, en
  D_Flip_Flop DQ (.clk(and_8_out), .D(or_3_out), .Q(DQ_q), .Qn(DQ_qn), .reset(button_1_out));  // open: preset, en
  D_Flip_Flop DR (.clk(and_8_out), .D(or_2_out), .Q(DR_q), .Qn(DR_qn), .reset(button_1_out));  // open: preset, en
  Button button_1 (.out(button_1_out));
  not not_1 (not_1_out, DP_q);
  not not_2 (not_2_out, DR_q);
  not not_3 (not_3_out, DQ_q);
  and and_9 (and_9_out, not_1_out, not_2_out);
  and and_10 (and_10_out, not_3_out, not_2_out);
  and and_11 (and_11_out, DQ_q, not_2_out);
  and and_12 (and_12_out, not_3_out, not_2_out);
  and and_13 (and_13_out, DP_q, not_3_out);
  and and_14 (and_14_out, DP_q, not_2_out);
  and and_15 (and_15_out, not_1_out, DQ_q);
  and and_16 (and_16_out, DQ_q, not_2_out);
  and and_17 (and_17_out, not_1_out, DQ_q);
  and and_18 (and_18_out, DQ_q, not_2_out);
  and and_19 (and_19_out, not_1_out, DQ_q);
  and and_20 (and_20_out, DQ_q, not_2_out);
  and and_21 (and_21_out, not_1_out, DR_q);
  and and_22 (and_22_out, DQ_q, not_2_out);
  or or_4 (or_4_out, not_1_out, and_10_out);
  or or_5 (or_5_out, not_1_out, and_11_out);
  or or_6 (or_6_out, and_12_out, and_13_out, and_14_out);
  or or_7 (or_7_out, and_9_out, and_15_out, and_16_out);
  or or_8 (or_8_out, and_17_out, and_18_out);
  or or_9 (or_9_out, and_19_out, and_20_out);
  or or_10 (or_10_out, and_21_out, and_22_out);
  _7_Segment_Display u_7_segment_display_1 (
    .g(or_6_out), .f(or_5_out), .a(or_7_out), .b(or_8_out), .e(or_4_out), .d(or_10_out), .c(or_9_out));  // open: dp
endmodule

module Basic_gate_using__T_Flip_Flop (
  input  Switch
);

  wire and_1_out, and_2_out, and_3_out, and_4_out, and_5_out, and_6_out, and_7_out, and_8_out, and_9_out,
       and_10_out, and_11_out, and_12_out, and_13_out, and_14_out, and_15_out, and_16_out, button_1_out,
       Clock_out, not_1_out, not_2_out, not_3_out, or_1_out, or_2_out, or_3_out, or_4_out, or_5_out,
       or_6_out, or_7_out, TP_q, TQ_q, TR_q;

  and and_1 (and_1_out, TQ_q, TR_q);
  and and_2 (and_2_out, Clock_out, Switch);
  T_Flip_Flop TP (.clk(and_2_out), .T(and_1_out), .Q(TP_q), .reset(button_1_out));  // open: Qn, preset, en
  T_Flip_Flop TQ (.clk(and_2_out), .T(TR_q), .Q(TQ_q), .reset(button_1_out));  // open: Qn, preset, en
  T_Flip_Flop TR (.clk(and_2_out), .T(1'b1), .Q(TR_q), .reset(button_1_out));  // open: Qn, preset, en
  Clock #(.highDuration(3), .lowDuration(2)) Clock (.out(Clock_out));
  Button button_1 (.out(button_1_out));
  not not_1 (not_1_out, TP_q);
  not not_2 (not_2_out, TQ_q);
  not not_3 (not_3_out, TR_q);
  and and_3 (and_3_out, not_2_out, not_3_out);
  and and_4 (and_4_out, not_1_out, not_3_out);
  and and_5 (and_5_out, not_1_out, TQ_q);
  and and_6 (and_6_out, not_1_out, TQ_q);
  and and_7 (and_7_out, TQ_q, not_3_out);
  and and_8 (and_8_out, not_1_out, TQ_q);
  and and_9 (and_9_out, TQ_q, not_3_out);
  and and_10 (and_10_out, not_1_out, TR_q);
  and and_11 (and_11_out, TQ_q, not_3_out);
  or or_1 (or_1_out, not_1_out, and_3_out);
  and and_12 (and_12_out, TQ_q, not_3_out);
  and and_13 (and_13_out, not_2_out, not_3_out);
  and and_14 (and_14_out, TP_q, not_2_out);
  and and_15 (and_15_out, TP_q, not_3_out);
  and and_16 (and_16_out, TQ_q, not_3_out);
  or or_2 (or_2_out, not_1_out, and_12_out);
  or or_3 (or_3_out, and_13_out, and_14_out, and_15_out);
  or or_4 (or_4_out, and_4_out, and_5_out, and_16_out);
  or or_5 (or_5_out, and_6_out, and_7_out);
  or or_6 (or_6_out, and_8_out, and_9_out);
  or or_7 (or_7_out, and_10_out, and_11_out);
  _7_Segment_Display u_7_segment_display_1 (
    .g(or_3_out), .f(or_2_out), .a(or_4_out), .b(or_5_out), .e(or_1_out), .d(or_7_out), .c(or_6_out));  // open: dp
endmodule

module Basic_gate_using__JK_Flip_Flop (
  input  Switch
);

  wire and_1_out, and_2_out, and_3_out, and_4_out, and_5_out, and_6_out, and_7_out, and_8_out, and_9_out,
       and_10_out, and_11_out, and_12_out, and_13_out, and_14_out, and_15_out, and_16_out, and_17_out,
       button_1_out, Clock_out, j_k_ff_1_q, j_k_ff_2_q, j_k_ff_3_q, not_1_out, not_2_out, not_3_out,
       or_1_out, or_2_out, or_3_out, or_4_out, or_5_out, or_6_out, or_7_out;

  and and_1 (and_1_out, j_k_ff_2_q, j_k_ff_3_q);
  and and_2 (and_2_out, j_k_ff_2_q, j_k_ff_3_q);
  and and_3 (and_3_out, Clock_out, Switch);
  J_K_Flip_Flop j_k_ff_1 (
    .J(and_1_out), .clk(and_3_out), .K(and_2_out), .Q(j_k_ff_1_q), .reset(button_1_out));  // open: Qn, preset, en
  J_K_Flip_Flop j_k_ff_2 (
    .J(j_k_ff_3_q), .clk(and_3_out), .K(j_k_ff_3_q), .Q(j_k_ff_2_q), .reset(button_1_out));  // open: Qn, preset, en
  J_K_Flip_Flop j_k_ff_3 (
    .J(1'b1), .clk(and_3_out), .K(1'b1), .Q(j_k_ff_3_q), .reset(button_1_out));  // open: Qn, preset, en
  Button button_1 (.out(button_1_out));
  Clock #(.highDuration(3), .lowDuration(2)) Clock (.out(Clock_out));
  not not_1 (not_1_out, j_k_ff_1_q);
  not not_2 (not_2_out, j_k_ff_3_q);
  not not_3 (not_3_out, j_k_ff_2_q);
  and and_4 (and_4_out, not_3_out, not_2_out);
  and and_5 (and_5_out, j_k_ff_2_q, not_2_out);
  and and_6 (and_6_out, not_1_out, not_2_out);
  and and_7 (and_7_out, not_1_out, j_k_ff_2_q);
  and and_8 (and_8_out, j_k_ff_2_q, not_2_out);
  and and_9 (and_9_out, not_1_out, j_k_ff_2_q);
  and and_10 (and_10_out, j_k_ff_2_q, not_2_out);
  and and_11 (and_11_out, not_1_out, j_k_ff_2_q);
  and and_12 (and_12_out, j_k_ff_2_q, not_2_out);
  and and_13 (and_13_out, not_1_out, j_k_ff_3_q);
  and and_14 (and_14_out, j_k_ff_2_q, not_2_out);
  or or_1 (or_1_out, not_1_out, and_4_out);
  or or_2 (or_2_out, not_1_out, and_5_out);
  and and_15 (and_15_out, not_3_out, not_2_out);
  and and_16 (and_16_out, j_k_ff_1_q, not_3_out);
  and and_17 (and_17_out, j_k_ff_1_q, not_2_out);
  or or_3 (or_3_out, and_6_out, and_7_out, and_8_out);
  or or_4 (or_4_out, and_9_out, and_10_out);
  or or_5 (or_5_out, and_11_out, and_12_out);
  or or_6 (or_6_out, and_13_out, and_14_out);
  or or_7 (or_7_out, and_15_out, and_16_out, and_17_out);
  _7_Segment_Display u_7_segment_display_1 (
    .g(or_7_out), .f(or_2_out), .a(or_3_out), .b(or_4_out), .e(or_1_out), .d(or_6_out), .c(or_5_out));  // open: dp

  // Notes on the sheet:
  //   JP
  //   KP
  //   JQ
  //   KQ
  //   JR
  //   KR
endmodule
